# Fritzing sketch alicidevre (saved by Fritzing 0.9.3b)
circuit board: 8.46667cm x 5.64444cm
breadboards: 1

parts:
  Parça1 = Arduino Nano (Rev3.0) (ICSP)
  IC3 = Voltage Regulator [package=78xxl]
  C1 = Capacitor Polarized [package=cpol-radial-100uf-25v]
  C2 = Ceramic Capacitor [capacitance=100nF package="100 mil [THT, multilayer]"]
  Parça2 = Triple Axis Accelerometer Breakout - ADXL345
  U1 = mystery part, 4 pins [chip_label=VERİCİ]
  R1 = Resistor [tolerance=±5% resistance=220 package=THT]
  LED1 = smd LED [color="Red (633nm)" package="0805 [SMD]"]
  ANT1 = Antenna
  VCC1 = Battery block 9V

nets:
  GND: Parça1.GND, IC3.GND, C1.-, C2.0, Parça2.GND, U1.pin2, LED1.cathode, VCC1.-
  N1: Parça1.D9, R1.Pin_0
  N2: Parça1.D12/MISO, U1.pin3
  N3: Parça1.VIN, IC3.OUT, C2.1, U1.pin1
  N4: Parça1.A5, Parça2.SCL
  N5: Parça1.A4, Parça2.SDA
  3V3: Parça1.3V3, Parça2.VCC
  N6: IC3.IN, C1.+, VCC1.+
  N7: U1.pin4, ANT1.antenna_lead
  N8: R1.Pin_1, LED1.anode

notes:
  1- VCC
  2- GND
  3- DATA
  4- ANTEN
  ADXL345 ivme sensöründen gelen x ve y değerlerine göre RF433 MHz Verici ile robotumuzun ileri, geri, sola, sağa ve durma hareket bilgileri Arduino Nanoda kodlanarak gönderilir.
